// Logisim project TME1.circ as structural Verilog: 5 circuits, main circuit mon_xor
module mon_xor (
  input  a,
  input  b,
  output out_3
);

  wire and_1_out, and_2_out;

  and and_1 (and_1_out, ~a, b);  // AND_Gate
  and and_2 (and_2_out, a, ~b);  // AND_Gate
  or or_1 (out_3, and_2_out, and_1_out);
endmodule

module mux2 (
  input  i,
  input  e0,
  input  e1,
  output out_4
);

  wire and_1_out, and_2_out, not_1_out;

  not not_1 (not_1_out, i);
  and and_1 (and_1_out, i, e1);
  and and_2 (and_2_out, not_1_out, e0);
  or or_1 (out_4, and_2_out, and_1_out);
endmodule

module mux2_4bits (
  input  i,
  input  a0,
  input  b0,
  input  a1,
  input  b1,
  input  a2,
  input  b2,
  input  a3,
  input  b3,
  output s0,
  output s1,
  output s2,
  output s3
);

  mux2 mux2_1 (.i(i), .e0(a0), .e1(b0), .out_4(s0));
  mux2 mux2_2 (.i(i), .e0(a1), .e1(b1), .out_4(s1));
  mux2 mux2_3 (.i(i), .e0(a2), .e1(b2), .out_4(s2));
  mux2 mux2_4 (.i(i), .e0(a3), .e1(b3), .out_4(s3));
endmodule

module mux4 (
  input  i1,
  input  e0,
  input  e1,
  input  i0,
  input  e2,
  input  e3,
  output s
);

  wire mux2_1_out_4, mux2_2_out_4;

  mux2 mux2_1 (.i(i0), .e0(e0), .e1(e1), .out_4(mux2_1_out_4));
  mux2 mux2_2 (.i(i0), .e0(e2), .e1(e3), .out_4(mux2_2_out_4));
  mux2 mux2_3 (.i(i1), .e0(mux2_1_out_4), .e1(mux2_2_out_4), .out_4(s));
endmodule

module comparateur (
  input  b2,
  input  a2,
  input  b1,
  input  a1,
  input  b0,
  input  a0,
  output s
);

  wire and_1_out, and_2_out, and_3_out, and_4_out, and_5_out, or_1_out, xnor_1_out, xnor_2_out;

  and and_1 (and_1_out, b2, ~a2);  // AND_Gate
  xnor xnor_1 (xnor_1_out, b2, a2);
  and and_2 (and_2_out, b1, ~a1);  // AND_Gate
  xnor xnor_2 (xnor_2_out, b1, a1);
  and and_3 (and_3_out, b0, ~a0);  // AND_Gate
  and and_4 (and_4_out, xnor_1_out, and_2_out);
  and and_5 (and_5_out, xnor_2_out, xnor_1_out, and_3_out);
  or or_1 (or_1_out, and_1_out, and_4_out);
  or or_2 (s, or_1_out, and_5_out);
endmodule
