// Logisim project TME2.circ as structural Verilog: 5 circuits, main circuit Additionneur_1bit
module Additionneur_1bit (
  input  Cin,
  input  A,
  input  B,
  output S,
  output Cout
);

  wire and_1_out, and_2_out, xor_1_out;

  xor xor_1 (xor_1_out, A, B);
  and and_1 (and_1_out, Cin, xor_1_out);
  and and_2 (and_2_out, A, B);
  xor xor_2 (S, Cin, xor_1_out);
  or or_1 (Cout, and_1_out, and_2_out);
endmodule

module Additionneur_4bits (
  input  in_1,
  input  A0,
  input  B0,
  input  A1,
  input  B1,
  input  A2,
  input  B2,
  input  A3,
  input  B3,
  output S0,
  output S1,
  output S2,
  output S3,
  output Cout
);

  wire additionneur_1bit_1_cout, additionneur_1bit_2_cout, additionneur_1bit_3_cout;

  Additionneur_1bit additionneur_1bit_1 (.A(A0), .B(B0), .Cin(in_1), .S(S0), .Cout(additionneur_1bit_1_cout));
  Additionneur_1bit additionneur_1bit_2 (
    .A(A1), .B(B1), .Cin(additionneur_1bit_1_cout), .S(S1), .Cout(additionneur_1bit_2_cout));
  Additionneur_1bit additionneur_1bit_3 (
    .A(A2), .B(B2), .Cin(additionneur_1bit_2_cout), .S(S2), .Cout(additionneur_1bit_3_cout));
  Additionneur_1bit additionneur_1bit_4 (.A(A3), .B(B3), .Cin(additionneur_1bit_3_cout), .S(S3), .Cout(Cout));
endmodule

module ALU__V1 (
  input  X0,
  input  Aluop,
  input  Y0,
  input  X1,
  input  Y1,
  input  X2,
  input  Y2,
  input  X3,
  input  Y3,
  output S0,
  output S1,
  output S2,
  output S3,
  output Cout
);

  wire multiplexer_1_out, multiplexer_2_out, multiplexer_3_out, multiplexer_4_out, not_1_out, not_2_out,
       not_3_out, not_4_out;

  Multiplexer #(.enable("false")) multiplexer_1 (.in0(Y0), .in1(not_1_out), .out(multiplexer_1_out), .sel(Aluop));
  not not_1 (not_1_out, Y0);
  Multiplexer #(.enable("false")) multiplexer_2 (.in0(Y1), .in1(not_2_out), .out(multiplexer_2_out), .sel(Aluop));
  not not_2 (not_2_out, Y1);
  Multiplexer #(.enable("false")) multiplexer_3 (.in0(Y2), .in1(not_3_out), .out(multiplexer_3_out), .sel(Aluop));
  not not_3 (not_3_out, Y2);
  Multiplexer #(.enable("false")) multiplexer_4 (.in0(Y3), .in1(not_4_out), .out(multiplexer_4_out), .sel(Aluop));
  not not_4 (not_4_out, Y3);
  Additionneur_4bits additionneur_4bits_1 (
    .A0(X0), .B0(multiplexer_1_out), .A1(X1), .B1(multiplexer_2_out), .A2(X2), .B2(multiplexer_3_out),
    .A3(X3), .B3(multiplexer_4_out), .in_1(Aluop), .S0(S0), .S1(S1), .S2(S2), .S3(S3), .Cout(Cout));
endmodule

module ALU_V2 (
  input  Aluop,
  input  X0,
  input  Y0,
  input  X1,
  input  Y1,
  input  X2,
  input  Y2,
  input  X3,
  input  Y3,
  output s0,
  output s1,
  output s2,
  output s3,
  output CF,
  output ZF,
  output SF,
  output OV
);

  wire additionneur_1bit_1_cout, additionneur_1bit_2_cout, additionneur_1bit_3_cout, multiplexer_1_out,
       multiplexer_2_out, multiplexer_3_out, multiplexer_4_out, not_1_out, not_2_out, not_3_out, not_4_out;

  Multiplexer #(.enable("false")) multiplexer_1 (.in0(Y0), .in1(not_1_out), .out(multiplexer_1_out), .sel(Aluop));
  not not_1 (not_1_out, Y0);
  Multiplexer #(.enable("false")) multiplexer_2 (.in0(Y1), .in1(not_2_out), .out(multiplexer_2_out), .sel(Aluop));
  not not_2 (not_2_out, Y1);
  Multiplexer #(.enable("false")) multiplexer_3 (.in0(Y2), .in1(not_3_out), .out(multiplexer_3_out), .sel(Aluop));
  not not_3 (not_3_out, Y2);
  Multiplexer #(.enable("false")) multiplexer_4 (.in0(Y3), .in1(not_4_out), .out(multiplexer_4_out), .sel(Aluop));
  not not_4 (not_4_out, Y3);
  Additionneur_1bit additionneur_1bit_1 (
    .A(X0), .B(multiplexer_1_out), .Cin(Aluop), .S(s0), .Cout(additionneur_1bit_1_cout));
  Additionneur_1bit additionneur_1bit_2 (
    .A(X1), .B(multiplexer_2_out), .Cin(additionneur_1bit_1_cout), .S(s1), .Cout(additionneur_1bit_2_cout));
  Additionneur_1bit additionneur_1bit_3 (
    .A(X2), .B(multiplexer_3_out), .Cin(additionneur_1bit_2_cout), .S(s2), .Cout(additionneur_1bit_3_cout));
  Additionneur_1bit additionneur_1bit_4 (
    .A(X3), .B(multiplexer_4_out), .Cin(additionneur_1bit_3_cout), .S(s3), .Cout(CF));
  or or_1 (SF, CF, Aluop);
  xor xor_1 (OV, additionneur_1bit_3_cout, CF);
  nor nor_1 (ZF, s0, s1, s2, s3);
endmodule

module Decalage (
  input  d1,
  input  d0,
  input  a0,
  input  a1,
  input  a2,
  input  a3,
  output s0,
  output s1,
  output s2,
  output s3
);

  wire and_2_out, and_3_out, and_4_out, and_5_out, and_6_out, and_7_out, and_8_out, and_9_out, and_10_out,
       not_1_out, not_2_out, not_3_out, not_4_out, not_5_out, not_6_out, not_7_out, not_8_out, not_9_out,
       not_10_out, not_11_out, not_12_out, not_13_out;

  not not_1 (not_1_out, d0);
  not not_2 (not_2_out, d1);
  not not_3 (not_3_out, d1);
  not not_4 (not_4_out, d0);
  not not_5 (not_5_out, d1);
  not not_6 (not_6_out, d0);
  not not_7 (not_7_out, d1);
  not not_8 (not_8_out, d1);
  not not_9 (not_9_out, d0);
  not not_10 (not_10_out, d0);
  not not_11 (not_11_out, d1);
  not not_12 (not_12_out, d0);
  not not_13 (not_13_out, d1);
  and and_1 (s0, a0, not_4_out, not_5_out);
  and and_2 (and_2_out, a1, not_1_out, not_2_out);
  and and_3 (and_3_out, a0, d0, not_3_out);
  and and_4 (and_4_out, a2, not_6_out, not_7_out);
  and and_5 (and_5_out, a1, d0, not_8_out);
  and and_6 (and_6_out, a0, not_9_out, d1);
  and and_7 (and_7_out, a3, not_10_out, not_11_out);
  and and_8 (and_8_out, a2, not_12_out, d1);
  and and_9 (and_9_out, a1, d0, not_13_out);
  and and_10 (and_10_out, a0, d0, d1);
  or or_1 (s2, and_4_out, and_5_out, and_6_out);
  or or_2 (s3, and_7_out, and_8_out, and_9_out, and_10_out);
  or or_3 (s1, and_2_out, and_3_out);
endmodule
